# Fritzing sketch Esquematica_obstaculo_morse (saved by Fritzing 1.0.2b)
breadboards: 1

parts:
  Componente2 = Arduino Uno (Rev3)-TopMount
  R1 = Resistor [tolerance=±5% resistance=220 package="0603 [SMD]"]
  R2 = Resistor [tolerance=±5% resistance=220 package="0603 [SMD]"]
  LED1 = LED - 3mm [color="Green (570nm)" current=0.030A package="3 mm [THT]"]
  LED2 = LED - 3mm [color="Red (633nm)" current=0.030A package="3 mm [THT]"]
  R3 = Resistor [tolerance=±5% resistance=220 package="0603 [SMD]"]
  A1 = Hiletgo 8digit led display
  R4 = Photocell (LDR) [power=0.25W dark_resistance_@0.01lx=300kΩ light_resistance_@100lx=400Ω luminance=10lx package=THT]

nets:
  N1: Componente2.A1, R3.Pin_1, R4.pin_0
  N2: Componente2.D12/MISO, LED2.anode
  N3: Componente2.D13/SCK, LED1.anode
  N4: Componente2.D5_PWM, A1.Pin_5, A1.Pin_6
  N5: Componente2.D6_PWM, A1.Pin_4
  N6: Componente2.D7, A1.Pin_3
  N7: Componente2.5V, R3.Pin_0, A1.Pin_1, A1.Pin_10
  N8: Componente2.GND, R1.Pin_0, R2.Pin_0, A1.Pin_2, A1.Pin_9, R4.pin_1
  N9: R1.Pin_1, LED1.cathode

notes:
  Usa o display de 4 bits

custom parts:
  Arduino Uno (Rev3)-TopMount: Arduino Uno (Rev3) for Top PCB Mount. The PCB view of the Arduino Uno (Rev3) in Arduino Bin flipped upside down with the text flipped back so as to be readable. Other views haven't changed Protruding component position is outlined to provide indication of part contact. Number in component outline is mm of protrusion of the component from the UNO PCB. Subtract the number from the USB (11mm),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
  Hiletgo 8digit led display: MAX7219 is an integrated serial input / output common-cathode display driver, which connects your microprocessor to a 7-segment digital LED display with 8 digits.
