# Fritzing sketch controle-micro (saved by Fritzing 1.0.2b)

parts:
  Componente1 = Bluetooth HC-05 Macho
  Componente3 = Arduino Mega ADK (Rev3)
  A1 = Electropeak 2.4in LCD  # not connected
  Componente4 = Black Joystick KY-023
  Mod1 = KY-004 Key Switch Module [package="Breakout board"]

nets:
  N1: Componente1.TXD, Componente3.D18/TX1
  N2: Componente1.RXD, Componente3.D19/RX1
  VCC: Componente1.VCC, Componente3.5V, Componente4.+5V, Mod1.S
  GND: Componente1.GND, Componente3.GND, Componente4.GND, Mod1.-
  N3: Componente3.A10, Componente4.VRx
  N4: Componente3.A11, Componente4.VRy
  N5: Componente3.D30, Mod1.Vin
  N6: Componente3.D40, Componente4.SW

custom parts:
  Electropeak 2.4in LCD: 2.4 inch Touch TFT LCD Display Shield for Arduino UNO/Mega.
  Black Joystick KY-023: Description: The joystick is a combination of 2 analoog potentiometer and a digital switch. Arduino GND --> Module pin - Arduino +5V --> Module pin +5V Arduino Analoog 0 --> Module VRx Arduino Analoog 1 --> Module VRy Arduino Digital --> Module SW Dimensions: 1" x 1.25"
  KY-004 Key Switch Module: Arduino Key Switch Module Keyes KY-004 is a push button that will output a high signal when pressed.
